# Fritzing sketch led_house (saved by Fritzing 0.9.4)
breadboards: 1

parts:
  Part1 = Arduino Uno (Rev3)
  LED1 = LED - 5mm [color="Red (633nm)" package="5 mm [THT]"]
  LED2 = LED - 5mm [color="Red (633nm)" package="5 mm [THT]"]
  LED3 = LED - 5mm [color="Red (633nm)" package="5 mm [THT]"]
  LED4 = LED - 5mm [color="Red (633nm)" package="5 mm [THT]"]
  LED5 = LED - 5mm [color="Red (633nm)" package="5 mm [THT]"]
  LED6 = LED - 5mm [color="Red (633nm)" package="5 mm [THT]"]
  LED7 = LED - 5mm [color="Red (633nm)" package="5 mm [THT]"]
  R1 = Resistor [tolerance=±5% resistance=220 package=THT]
  R2 = Resistor [tolerance=±5% resistance=220 package=THT]
  R3 = Resistor [tolerance=±5% resistance=220 package=THT]
  R4 = Resistor [tolerance=±5% resistance=220 package=THT]
  R5 = Resistor [tolerance=±5% resistance=220 package=THT]
  R6 = Resistor [tolerance=±5% resistance=220 package=THT]
  R7 = Resistor [tolerance=±5% resistance=220 package=THT]
  U3 = RELAY [package=OJ]
  U4 = RELAY [package=OJ]
  R8 = Resistor [tolerance=±5% resistance=220 package=THT]
  R9 = Resistor [tolerance=±5% resistance=220 package=THT]
  S1 = Pushbutton [package=THT]
  S2 = Pushbutton [package=THT]

nets:
  RELAY1: Part1.D10_PWM/SS, U3.NO
  RELAY2: Part1.D11_PWM/MOSI, U4.NO
  BTN_A: Part1.D12/MISO, R8.Pin_0
  BTN_B: Part1.D13/SCK, R9.Pin_0
  LED1: Part1.D1/TX, R1.Pin_0
  LED2: Part1.D2, R2.Pin_0
  LED3: Part1.D3_PWM, R3.Pin_0
  LED4: Part1.D4, R4.Pin_0
  LED5: Part1.D5_PWM, R5.Pin_0
  LED6: Part1.D6_PWM, R6.Pin_0
  LED7: Part1.D7, R7.Pin_0
  GND: LED1.cathode, LED2.cathode, LED3.cathode, LED4.cathode, LED5.cathode, LED6.cathode, LED7.cathode, U3.MAIN, U4.MAIN, S1.leg1, S2.leg1
  N1: LED1.anode, R1.Pin_1
  N2: LED2.anode, R2.Pin_1
  N3: LED3.anode, R3.Pin_1
  N4: LED4.anode, R5.Pin_1
  N5: LED5.anode, R4.Pin_1
  N6: LED6.anode, R6.Pin_1
  N7: LED7.anode, R7.Pin_1
  N8: R8.Pin_1, S1.leg0
  N9: R9.Pin_1, S2.leg0

// code stored in the sketch: test_wrk.ino
// LEDS
const int LED1 = 1;
const int LED2 = 2;
const int LED3 = 3;
const int LED4 = 4;
const int LED5 = 5;
const int LED6 = 6;
const int LED7 = 7;

// RELAYS
const int RELAY1 = 10;
const int RELAY2 = 11;

// BUTTONS
const int BTN_A = 12;
const int BTN_B = 13;

int timer_hours = 1; // 1h
unsigned long timer;

// 0 - manual off
// 1 - manual on
// 2 - manual auto
int manual_states = 0;

int button_b_states = 0;

void setup() {

  // Initialize leds
  pinMode(LED1, OUTPUT);
  pinMode(LED2, OUTPUT);
  pinMode(LED3, OUTPUT);
  pinMode(LED4, OUTPUT);
  pinMode(LED5, OUTPUT);
  pinMode(LED6, OUTPUT);
  pinMode(LED7, OUTPUT);

  // Initialize Realys
  pinMode(RELAY1, OUTPUT);
  pinMode(RELAY2, OUTPUT);

  // Initialize buttons
  pinMode(BTN_A, INPUT);
  pinMode(BTN_B, INPUT);

  timer = millis();
}

void loop() {

  if (button_A_pressed()) {
    manual_states++;
    delay(1000);
    if (manual_states > 3) {
      manual_states = 0; // RECYCLE
    }

    switch (manual_states) {
      case 0 : digitalWrite(LED1, HIGH); break; // YELLOW
      case 1 : digitalWrite(LED1, HIGH); break; // GREEN
    }
  }

  if (millis() >= getHours() && manual_states == 0) {
    timer = millis();
  }

  if (manual_states == 2 && button_B_pressed()) {
    button_b_states++;
    delay(1000);
    if (button_b_states > 4) {
      button_b_states = 0; // RECYCLE
    }

    all_off();
    switch (button_b_states) {
      case 0 : {
          digitalWrite(LED2, HIGH);
          digitalWrite(LED3, HIGH);
          break;
        }
      case 1 : {
          digitalWrite(LED4, HIGH);
          digitalWrite(LED5, HIGH);
          break;
        }
      case 2 : {
          digitalWrite(LED1, HIGH);
          digitalWrite(LED2, HIGH);
          digitalWrite(LED3, HIGH);
          digitalWrite(LED4, HIGH);
          digitalWrite(LED5, HIGH);
          digitalWrite(LED6, HIGH);
          digitalWrite(LED7, HIGH);
          break;
        }
      case 3 : {
          digitalWrite(LED1, HIGH);
          digitalWrite(LED2, HIGH);
          digitalWrite(LED3, HIGH);
          digitalWrite(LED4, HIGH);
          digitalWrite(LED5, HIGH);
          digitalWrite(LED6, HIGH);
          digitalWrite(LED7, HIGH);

          digitalWrite(RELAY1, HIGH);
          break;
        }
      case 4 : {
          digitalWrite(LED1, HIGH);
          digitalWrite(LED2, HIGH);
          digitalWrite(LED3, HIGH);
          digitalWrite(LED4, HIGH);
          digitalWrite(LED5, HIGH);
          digitalWrite(LED6, HIGH);
          digitalWrite(LED7, HIGH);

          digitalWrite(RELAY2, HIGH);
          break;
        }
    }
  }

}
long getHours() {
  return 3600L * 1000 * timer_hours;
}
bool button_A_pressed() {
  return digitalRead(BTN_A);
}
bool button_B_pressed() {
  return digitalRead(BTN_B);
}
void all_off() {
  digitalWrite(LED1, LOW);
  digitalWrite(LED2, LOW);
  digitalWrite(LED3, LOW);
  digitalWrite(LED4, LOW);
  digitalWrite(LED5, LOW);
  digitalWrite(LED6, LOW);
  digitalWrite(LED7, LOW);

  digitalWrite(RELAY1, LOW);
  digitalWrite(RELAY2, LOW);
}
